# Fritzing sketch Untitled Sketch 2 (saved by Fritzing 0.9.2b)
breadboards: 1

parts:
  Part1 = Arduino Nano (Rev3.0)
  Part2 = HX711 Weighing Sensor Module
  BT1 = Bluetooth HC-06d [package=THT]
  Part3 = LCD1602-I2C
  BATT1 = 4xAA Switchable Battery Pack w/Bare Wire
  Input1 = Load Sensor
  Input2 = Load Sensor
  Input3 = Load Sensor
  Input4 = Load Sensor

nets:
  GND: Part1.GND, BT1.GND, BATT1.NEG
  N1: Part1.D2, Part2.DO/RX
  N2: Part1.D3, Part2.CK/TX
  N3: Part1.D6, BT1.RXD
  N4: Part1.D7, BT1.TXD
  N5: Part1.VIN, BATT1.POS
  VCC: Part1.5V, BT1.VCC, Part3.VCC
  N6: Part1.A5, Part3.SCL
  N7: Part1.A4, Part3.SDA
  GND_2: Part2.E+, Part2.E-, Part2.A+, Part2.A-, Input1.Sense_(V-), Input1.GND, Input1.Power, Input2.Power, Input3.Power, Input4.GND, Input4.Power

custom parts:
  Bluetooth HC-06d: Bluetooth HC-06 - face down, pins down 16.5mm x 37.5mm PCB
  LCD1602-I2C: A standard character display, usually with 2x16 characters. Comes in many colors with LCM1602 IIC attached.
  4xAA Switchable Battery Pack w/Bare Wire: 4xAA Switchable Battery Pack with Bare Wire connection
  Load Sensor: 3-Wire Load Cell, a half wheatstone bridge.
